// Logisim project Digital_Data_Transmission_Error_Detection (1).circ as structural Verilog: 1 circuit, main circuit main
module main (
  input  T3,
  input  T2,
  input  T1,
  input  T0,
  input  R3,
  input  R2,
  input  R1,
  input  R0,
  output ERROR_DETECED,
  output NO_ERROR
);

  wire XOR_2_out, XOR_3_out, XOR_4_out, XOR_out;

  xor XOR (XOR_out, T3, T2);
  xor XOR_2 (XOR_2_out, T1, T0);
  xor XOR_3 (XOR_3_out, R3, R2);
  xor XOR_4 (XOR_4_out, R1, R0);
  or OR (ERROR_DETECED, XOR_out, XOR_2_out, XOR_3_out, XOR_4_out);
  not NOT (NO_ERROR, ERROR_DETECED);
endmodule
